// Logisim project 6651071003_LAB2_3.circ as structural Verilog: 2 circuits, main circuit main
module main (
  input  [3:0] A_3_0,
  input  [3:0] B_3_0,
  output [3:0] Sum_3_0
);

  wire T0_cout, T1_cout, T2_cout;

  _1bitFA T0 (.A(A_3_0[0]), .B(B_3_0[0]), .Cin(1'b0), .Sum(Sum_3_0[0]), .Cout(T0_cout));
  _1bitFA T1 (.A(A_3_0[1]), .B(B_3_0[1]), .Cin(T0_cout), .Sum(Sum_3_0[1]), .Cout(T1_cout));
  _1bitFA T2 (.A(A_3_0[2]), .B(B_3_0[2]), .Cin(T1_cout), .Sum(Sum_3_0[2]), .Cout(T2_cout));
  _1bitFA T3 (.A(A_3_0[3]), .B(B_3_0[3]), .Cin(T2_cout), .Sum(Sum_3_0[3]));  // open: Cout
endmodule

module _1bitFA (
  input  A,
  input  B,
  input  Cin,
  output Sum,
  output Cout
);

  wire and_1_out, and_2_out, xor_1_out;

  xor xor_1 (xor_1_out, A, B);
  and and_1 (and_1_out, A, B);
  xor xor_2 (Sum, xor_1_out, Cin);
  and and_2 (and_2_out, xor_1_out, Cin);
  or or_1 (Cout, and_1_out, and_2_out);
endmodule
