// Logisim project 6651071003_LAB2_4.circ as structural Verilog: 1 circuit, main circuit main
module main (
  input  [3:0] A,
  input  [3:0] B,
  output [3:0] Difference,
  output Borrow
);

  wire adder_1_cout;
  wire [3:0] not_1_out;

  assign not_1_out = ~B;  // NOT_Gate not_1, 4 bits wide
  Adder #(.width(4)) adder_1 (.a(A), .b(not_1_out), .out(Difference), .cin(1'b1), .cout(adder_1_cout));
  not not_2 (Borrow, adder_1_cout);
endmodule
