// Logisim project 6651071003_LAB2_5.circ as structural Verilog: 1 circuit, main circuit main
module main (
  input  [3:0] A,
  input  [3:0] B,
  output A_B,
  output A_B_2,
  output A_B_3
);

  Comparator #(.width(4), .mode("unsigned")) comparator_1 (.a(A), .b(B), .gt(A_B), .eq(A_B_2), .lt(A_B_3));
endmodule
