// Logisim project 6651071003_LAB2_6.circ as structural Verilog: 1 circuit, main circuit main
module main (
  input  Reset,
  output Q0,
  output Q1,
  output Q2,
  output Q3
);

  wire clock_1_out, FF0_qn, FF1_qn, FF2_qn;

  J_K_Flip_Flop FF0 (.J(1'b1), .K(1'b1), .Q(Q0), .Qn(FF0_qn), .preset(clock_1_out), .reset(FF0_qn));  // open: clk, en
  J_K_Flip_Flop FF1 (.J(1'b1), .K(1'b1), .Q(Q1), .Qn(FF1_qn), .preset(FF0_qn), .reset(FF1_qn));  // open: clk, en
  J_K_Flip_Flop FF2 (.J(1'b1), .K(1'b1), .Q(Q2), .Qn(FF2_qn), .preset(FF1_qn), .reset(FF2_qn));  // open: clk, en
  J_K_Flip_Flop FF3 (.J(1'b1), .K(1'b1), .Q(Q3), .preset(FF2_qn), .reset(Reset));  // open: clk, Qn, en
  Clock clock_1 (.out(clock_1_out));
endmodule
