// Logisim project 6651071003_LAB2_7.circ as structural Verilog: 1 circuit, main circuit main
module main (
  input  [3:0] Data_in,
  input  [2:0] Addr,
  input  Write_Enable,
  output [3:0] Data_out
);

  wire clock_1_out, not_1_out;

  Clock clock_1 (.out(clock_1_out));
  RAM #(.addrWidth(3), .dataWidth(4)) ram_1 (
    .addr(Addr), .data(Data_out), .sel(1'b1), .clk(clock_1_out), .ld(not_1_out));  // open: clr
  not not_1 (not_1_out, Write_Enable);
  assign Data_out = Write_Enable ? Data_in : 4'bz;  // Controlled_Buffer controlled_buffer_1
endmodule
